// Logisim project Darkstar.circ as structural Verilog: 11 circuits, main circuit main
module main (
  input  Reset
);

  wire Arithmetic_Engine_c, Arithmetic_Engine_n, Arithmetic_Engine_v, Arithmetic_Engine_z, beq_out, bge_out,
       bgeu_out, blt_out, bltu_out, bne_out, Branch_out, Clk_out, CU_auipc, CU_b_src, CU_beq, CU_bge,
       CU_bgeu, CU_blt, CU_bltu, CU_bne, CU_jal, CU_jalr, CU_lui, CU_memread, CU_memsigned, CU_memwrite,
       CU_negate, CU_regwrite, CU_wordflag, not_1_out, not_2_out, not_3_out, or_1_out, or_2_out, or_3_out,
       or_4_out, PC_Adder_cout, xor_1_out;
  wire [1:0] CU_memsize;
  wire [2:0] CU_alu_op;
  wire [11:0] multiplexer_4_out;
  wire [63:0] Arithmetic_Engine_result, bit_extender_1_out, bit_extender_2_out, bit_extender_3_out,
       bit_extender_4_out, Data_data_out, Instructions_instr, Internal_Registers_pc_out,
       Internal_Registers_reg1_out, Internal_Registers_reg2_out, multiplexer_1_out, multiplexer_2_out,
       multiplexer_3_out, multiplexer_5_out, multiplexer_6_out, multiplexer_7_out, multiplexer_8_out,
       multiplexer_9_out, multiplexer_10_out, multiplexer_11_out, multiplexer_12_out, PC_Adder_s;

  Clock Clk (.out(Clk_out));
  Multiplexer #(.width(64)) multiplexer_1 (
    .in0(64'h4), .in1(multiplexer_7_out), .out(multiplexer_1_out), .sel(or_1_out));
  or or_1 (or_1_out, Branch_out, CU_jal);
  Program_Memory Instructions (.PC(Internal_Registers_pc_out), .Instr(Instructions_instr));
  CLA64 PC_Adder (
    .A(Internal_Registers_pc_out), .B(multiplexer_1_out), .Cin(1'b0), .S(PC_Adder_s), .Cout(PC_Adder_cout));
  // NoConnect on PC_Adder_cout
  assign bit_extender_1_out = {{51{Instructions_instr[31]}}, {Instructions_instr[31], Instructions_instr[7], Instructions_instr[30:25], Instructions_instr[11:8], 1'b0}};  // Bit_Extender bit_extender_1
  assign bit_extender_2_out = {{32{Instructions_instr[31]}}, {Instructions_instr[31:12], {12{1'b0}}}};  // Bit_Extender bit_extender_2
  assign bit_extender_3_out = {{43{Instructions_instr[31]}}, {Instructions_instr[31], Instructions_instr[19:12], Instructions_instr[20], Instructions_instr[30:21], 1'b0}};  // Bit_Extender bit_extender_3
  Multiplexer #(.width(64)) multiplexer_2 (
    .in0(multiplexer_12_out), .in1(PC_Adder_s), .out(multiplexer_2_out), .sel(CU_jalr));
  Multiplexer #(.width(64)) multiplexer_3 (
    .in0(PC_Adder_s), .in1({multiplexer_12_out[63:1], 1'b0}), .out(multiplexer_3_out), .sel(CU_jalr));
  Control_Unit CU (
    .Op(Instructions_instr[6:0]), .funct3(Instructions_instr[14:12]), .funct7_5(Instructions_instr[30]),
    .ALU_Op(CU_alu_op), .Negate(CU_negate), .RegWrite(CU_regwrite), .B_Src(CU_b_src),
    .MemSigned(CU_memsigned), .MemWrite(CU_memwrite), .MemRead(CU_memread), .MemSize(CU_memsize),
    .BEQ(CU_beq), .BNE(CU_bne), .BLT(CU_blt), .BGE(CU_bge), .BLTU(CU_bltu), .BGEU(CU_bgeu), .LUI(CU_lui),
    .AUIPC(CU_auipc), .JAL(CU_jal), .JALR(CU_jalr), .WordFlag(CU_wordflag));  // open: Valid
  Multiplexer #(.width(12)) multiplexer_4 (
    .in0(Instructions_instr[31:20]), .in1({Instructions_instr[31:25], Instructions_instr[11:7]}),
    .out(multiplexer_4_out), .sel(CU_memwrite));
  assign bit_extender_4_out = {{52{multiplexer_4_out[11]}}, multiplexer_4_out};  // Bit_Extender bit_extender_4
  or or_2 (or_2_out, CU_bgeu, CU_bltu, CU_bge, CU_blt, CU_bne, CU_beq);
  or or_3 (or_3_out, CU_auipc, CU_lui);
  Multiplexer #(.width(64)) multiplexer_5 (
    .in0(bit_extender_4_out), .in1(bit_extender_1_out), .out(multiplexer_5_out), .sel(or_2_out));
  Regfile Internal_Registers (
    .Read_Register1(Instructions_instr[19:15]), .Read_Register2(Instructions_instr[24:20]),
    .Write_Data(multiplexer_2_out), .Clock(Clk_out), .Reset(Reset),
    .Write_Register(Instructions_instr[11:7]), .Write_Enable(CU_regwrite), .PC_In(multiplexer_3_out),
    .Reg1_Out(Internal_Registers_reg1_out), .Reg2_Out(Internal_Registers_reg2_out),
    .PC_Out(Internal_Registers_pc_out));
  Multiplexer #(.width(64)) multiplexer_6 (
    .in0(multiplexer_5_out), .in1(bit_extender_2_out), .out(multiplexer_6_out), .sel(or_3_out));
  Multiplexer #(.width(64)) multiplexer_7 (
    .in0(multiplexer_6_out), .in1(bit_extender_3_out), .out(multiplexer_7_out), .sel(CU_jal));
  Multiplexer #(.width(64)) multiplexer_8 (
    .in0(Internal_Registers_reg2_out), .in1(multiplexer_7_out), .out(multiplexer_8_out), .sel(CU_b_src));
  or or_4 (or_4_out, CU_auipc, CU_jal);
  Multiplexer #(.width(64)) multiplexer_9 (
    .in0(Internal_Registers_reg1_out), .in1({64{1'b0}}), .out(multiplexer_9_out), .sel(CU_lui));
  Multiplexer #(.width(64)) multiplexer_10 (
    .in0(multiplexer_8_out), .in1(64'h4), .out(multiplexer_10_out), .sel(CU_jal));
  Multiplexer #(.width(64)) multiplexer_11 (
    .in0(multiplexer_9_out), .in1(Internal_Registers_pc_out), .out(multiplexer_11_out), .sel(or_4_out));
  Multiplexer #(.width(64)) multiplexer_12 (
    .in0(Arithmetic_Engine_result), .in1(Data_data_out), .out(multiplexer_12_out), .sel(CU_memread));
  ALU Arithmetic_Engine (
    .A(multiplexer_11_out), .B(multiplexer_10_out), .ALU_Op(CU_alu_op), .Negate(CU_negate),
    .WordFlag(CU_wordflag), .Result(Arithmetic_Engine_result), .N(Arithmetic_Engine_n),
    .Z(Arithmetic_Engine_z), .C(Arithmetic_Engine_c), .V(Arithmetic_Engine_v));
  not not_1 (not_1_out, Arithmetic_Engine_z);
  xor xor_1 (xor_1_out, Arithmetic_Engine_n, Arithmetic_Engine_v);
  not not_2 (not_2_out, Arithmetic_Engine_c);
  and beq (beq_out, CU_beq, Arithmetic_Engine_z);
  and bne (bne_out, CU_bne, not_1_out);
  and blt (blt_out, CU_blt, xor_1_out);
  and bge (bge_out, CU_bge, not_3_out);
  not not_3 (not_3_out, xor_1_out);
  and bltu (bltu_out, CU_bltu, not_2_out);
  and bgeu (bgeu_out, CU_bgeu, Arithmetic_Engine_c);
  or Branch (Branch_out, beq_out, bne_out, blt_out, bge_out, bltu_out, bgeu_out);
  Data_Memory Data (
    .Reset(Reset), .Unsigned0_Signed1(CU_memsigned), .Address(Arithmetic_Engine_result), .Store(CU_memwrite),
    .Load(CU_memread), .Clock(Clk_out), .Data_In(Internal_Registers_reg2_out), .Size_Flag(CU_memsize),
    .Data_Out(Data_data_out));

  // Notes on the sheet:
  //   I-Type Immediate
  //   S-Type Immediate
  //   B-Type Immediate
  //   Upper Immediate
  //   JAL Immediate
endmodule

module Control_Unit (
  input  [6:0] Op,
  input  [2:0] funct3,
  input  funct7_5,
  output [2:0] ALU_Op,
  output Negate,
  output RegWrite,
  output B_Src,
  output MemSigned,
  output MemWrite,
  output MemRead,
  output [1:0] MemSize,
  output BEQ,
  output BNE,
  output BLT,
  output BGE,
  output BLTU,
  output BGEU,
  output LUI,
  output AUIPC,
  output JAL,
  output JALR,
  output WordFlag,
  output Valid
);

  ROM #(.addrWidth(11), .dataWidth(23)) Decoding_ROM (
    .addr({funct7_5, funct3, Op}),
    .data({Valid, WordFlag, JALR, JAL, AUIPC, LUI, BGEU, BLTU, BGE, BLT, BNE, BEQ, MemSize, MemRead, MemWrite, MemSigned, B_Src, RegWrite, Negate, ALU_Op}));

  // Notes on the sheet:
  //   contents of Decoding_ROM (hex, n*v repeats v):
  //   0 0 0 400170 15*0 400030 0 0 0 440030 0 0 0 600030 7*0 4000a0 15*0 400010 0 0 0 420030 0 0 0 600010
  //   39*0 400808 0 0 0 500030 7*0 480030 19*0 400370 15*0 400031 0 0 0 440030 0 0 0 600031 7*0 4002a0
  //   15*0 400011 0 0 0 420030 0 0 0 600011 39*0 401008 11*0 480030 19*0 400570 15*0 40003a 0 0 0 440030
  //   11*0 4004a0 15*0 40001a 0 0 0 420030 55*0 480030 19*0 400730 15*0 40003b 0 0 0 440030 11*0 4006a0
  //   15*0 40001b 0 0 0 420030 55*0 480030 19*0 400130 15*0 400034 0 0 0 440030 27*0 400014 0 0 0 420030
  //   43*0 402008 11*0 480030 19*0 400330 15*0 400035 0 0 0 440030 0 0 0 600035 23*0 400015 0 0 0 420030 0
  //   0 0 600015 39*0 404008 11*0 480030 19*0 400530 15*0 400036 0 0 0 440030 27*0 400016 0 0 0 420030
  //   43*0 408008 11*0 480030 35*0 400037 0 0 0 440030 27*0 400017 0 0 0 420030 43*0 410008 11*0 480030
  //   19*0 400170 15*0 400030 0 0 0 440030 0 0 0 600030 7*0 4000a0 15*0 400018 0 0 0 420030 0 0 0 600018
  //   39*0 400808 0 0 0 500030 7*0 480030 19*0 400370 19*0 440030 11*0 4002a0 19*0 420030 43*0 401008 11*0
  //   480030 19*0 400570 15*0 40003a 0 0 0 440030 11*0 4004a0 19*0 420030 55*0 480030 19*0 400730 15*0
  //   40003b 0 0 0 440030 11*0 4006a0 19*0 420030 55*0 480030 19*0 400130 15*0 400034 0 0 0 440030 31*0
  //   420030 43*0 402008 11*0 480030 19*0 400330 15*0 40003d 0 0 0 440030 0 0 0 60003d 23*0 40001d 0 0 0
  //   420030 0 0 0 60001d 39*0 404008 11*0 480030 19*0 400530 15*0 400036 0 0 0 440030 31*0 420030 43*0
  //   408008 11*0 480030 35*0 400037 0 0 0 440030 31*0 420030 43*0 410008 11*0 480030
endmodule

module Regfile (
  input  [4:0] Read_Register1,
  input  [4:0] Read_Register2,
  input  [63:0] Write_Data,
  input  Clock,
  input  Reset,
  input  [4:0] Write_Register,
  input  Write_Enable,
  input  [63:0] PC_In,
  output [63:0] Reg1_Out,
  output [63:0] Reg2_Out,
  output [63:0] PC_Out
);

  wire decoder_1_out1, decoder_1_out2, decoder_1_out3, decoder_1_out4, decoder_1_out5, decoder_1_out6,
       decoder_1_out7, decoder_1_out8, decoder_1_out9, decoder_1_out10, decoder_1_out11, decoder_1_out12,
       decoder_1_out13, decoder_1_out14, decoder_1_out15, decoder_1_out16, decoder_1_out17, decoder_1_out18,
       decoder_1_out19, decoder_1_out20, decoder_1_out21, decoder_1_out22, decoder_1_out23, decoder_1_out24,
       decoder_1_out25, decoder_1_out26, decoder_1_out27, decoder_1_out28, decoder_1_out29, decoder_1_out30,
       decoder_1_out31;
  wire [63:0] x0_q, x1_q, x2_q, x3_q, x4_q, x5_q, x6_q, x7_q, x8_q, x9_q, x10_q, x11_q, x12_q, x13_q, x14_q,
       x15_q, x16_q, x17_q, x18_q, x19_q, x20_q, x21_q, x22_q, x23_q, x24_q, x25_q, x26_q, x27_q, x28_q,
       x29_q, x30_q, x31_q;

  Decoder #(.select(5)) decoder_1 (
    .out1(decoder_1_out1), .out2(decoder_1_out2), .out3(decoder_1_out3), .out4(decoder_1_out4),
    .out5(decoder_1_out5), .out6(decoder_1_out6), .out7(decoder_1_out7), .out8(decoder_1_out8),
    .out9(decoder_1_out9), .out10(decoder_1_out10), .out11(decoder_1_out11), .out12(decoder_1_out12),
    .out13(decoder_1_out13), .out14(decoder_1_out14), .out15(decoder_1_out15), .out16(decoder_1_out16),
    .out17(decoder_1_out17), .out18(decoder_1_out18), .out19(decoder_1_out19), .out20(decoder_1_out20),
    .out21(decoder_1_out21), .out22(decoder_1_out22), .out23(decoder_1_out23), .out24(decoder_1_out24),
    .out25(decoder_1_out25), .out26(decoder_1_out26), .out27(decoder_1_out27), .out28(decoder_1_out28),
    .out29(decoder_1_out29), .out30(decoder_1_out30), .out31(decoder_1_out31), .sel(Write_Register),
    .en(Write_Enable));  // open: out0
  Register #(.width(64)) x0 (.en(1'b0), .clk(Clock), .Q(x0_q), .clr(Reset));  // open: D
  Register #(.width(64)) x1 (.D(Write_Data), .en(decoder_1_out1), .clk(Clock), .Q(x1_q), .clr(Reset));
  Register #(.width(64)) x2 (.D(Write_Data), .en(decoder_1_out2), .clk(Clock), .Q(x2_q), .clr(Reset));
  Register #(.width(64)) x3 (.D(Write_Data), .en(decoder_1_out3), .clk(Clock), .Q(x3_q), .clr(Reset));
  Register #(.width(64)) x4 (.D(Write_Data), .en(decoder_1_out4), .clk(Clock), .Q(x4_q), .clr(Reset));
  Register #(.width(64)) x5 (.D(Write_Data), .en(decoder_1_out5), .clk(Clock), .Q(x5_q), .clr(Reset));
  Register #(.width(64)) x6 (.D(Write_Data), .en(decoder_1_out6), .clk(Clock), .Q(x6_q), .clr(Reset));
  Register #(.width(64)) x7 (.D(Write_Data), .en(decoder_1_out7), .clk(Clock), .Q(x7_q), .clr(Reset));
  Register #(.width(64)) x8 (.D(Write_Data), .en(decoder_1_out8), .clk(Clock), .Q(x8_q), .clr(Reset));
  Register #(.width(64)) x9 (.D(Write_Data), .en(decoder_1_out9), .clk(Clock), .Q(x9_q), .clr(Reset));
  Register #(.width(64)) x10 (.D(Write_Data), .en(decoder_1_out10), .clk(Clock), .Q(x10_q), .clr(Reset));
  Register #(.width(64)) x11 (.D(Write_Data), .en(decoder_1_out11), .clk(Clock), .Q(x11_q), .clr(Reset));
  Register #(.width(64)) x12 (.D(Write_Data), .en(decoder_1_out12), .clk(Clock), .Q(x12_q), .clr(Reset));
  Register #(.width(64)) x13 (.D(Write_Data), .en(decoder_1_out13), .clk(Clock), .Q(x13_q), .clr(Reset));
  Register #(.width(64)) x14 (.D(Write_Data), .en(decoder_1_out14), .clk(Clock), .Q(x14_q), .clr(Reset));
  Register #(.width(64)) x15 (.D(Write_Data), .en(decoder_1_out15), .clk(Clock), .Q(x15_q), .clr(Reset));
  Register #(.width(64)) x16 (.D(Write_Data), .en(decoder_1_out16), .clk(Clock), .Q(x16_q), .clr(Reset));
  Register #(.width(64)) x17 (.D(Write_Data), .en(decoder_1_out17), .clk(Clock), .Q(x17_q), .clr(Reset));
  Register #(.width(64)) x18 (.D(Write_Data), .en(decoder_1_out18), .clk(Clock), .Q(x18_q), .clr(Reset));
  Register #(.width(64)) x19 (.D(Write_Data), .en(decoder_1_out19), .clk(Clock), .Q(x19_q), .clr(Reset));
  Register #(.width(64)) x20 (.D(Write_Data), .en(decoder_1_out20), .clk(Clock), .Q(x20_q), .clr(Reset));
  Register #(.width(64)) x21 (.D(Write_Data), .en(decoder_1_out21), .clk(Clock), .Q(x21_q), .clr(Reset));
  Register #(.width(64)) x22 (.D(Write_Data), .en(decoder_1_out22), .clk(Clock), .Q(x22_q), .clr(Reset));
  Register #(.width(64)) x23 (.D(Write_Data), .en(decoder_1_out23), .clk(Clock), .Q(x23_q), .clr(Reset));
  Register #(.width(64)) x24 (.D(Write_Data), .en(decoder_1_out24), .clk(Clock), .Q(x24_q), .clr(Reset));
  Register #(.width(64)) x25 (.D(Write_Data), .en(decoder_1_out25), .clk(Clock), .Q(x25_q), .clr(Reset));
  Register #(.width(64)) x26 (.D(Write_Data), .en(decoder_1_out26), .clk(Clock), .Q(x26_q), .clr(Reset));
  Register #(.width(64)) x27 (.D(Write_Data), .en(decoder_1_out27), .clk(Clock), .Q(x27_q), .clr(Reset));
  Register #(.width(64)) x28 (.D(Write_Data), .en(decoder_1_out28), .clk(Clock), .Q(x28_q), .clr(Reset));
  Register #(.width(64)) x29 (.D(Write_Data), .en(decoder_1_out29), .clk(Clock), .Q(x29_q), .clr(Reset));
  Register #(.width(64)) x30 (.D(Write_Data), .en(decoder_1_out30), .clk(Clock), .Q(x30_q), .clr(Reset));
  Register #(.width(64)) x31 (.D(Write_Data), .en(decoder_1_out31), .clk(Clock), .Q(x31_q), .clr(Reset));
  Register #(.width(64)) pc (.D(PC_In), .en(1'b1), .clk(Clock), .Q(PC_Out), .clr(Reset));
  Multiplexer #(.select(5), .width(64)) multiplexer_1 (
    .in0(x0_q), .in1(x1_q), .in2(x2_q), .in3(x3_q), .in4(x4_q), .in5(x5_q), .in6(x6_q), .in7(x7_q),
    .in8(x8_q), .in9(x9_q), .in10(x10_q), .in11(x11_q), .in12(x12_q), .in13(x13_q), .in14(x14_q),
    .in15(x15_q), .in16(x16_q), .in17(x17_q), .in18(x18_q), .in19(x19_q), .in20(x20_q), .in21(x21_q),
    .in22(x22_q), .in23(x23_q), .in24(x24_q), .in25(x25_q), .in26(x26_q), .in27(x27_q), .in28(x28_q),
    .in29(x29_q), .in30(x30_q), .in31(x31_q), .out(Reg1_Out), .sel(Read_Register1));
  Multiplexer #(.select(5), .width(64)) multiplexer_2 (
    .in0(x0_q), .in1(x1_q), .in2(x2_q), .in3(x3_q), .in4(x4_q), .in5(x5_q), .in6(x6_q), .in7(x7_q),
    .in8(x8_q), .in9(x9_q), .in10(x10_q), .in11(x11_q), .in12(x12_q), .in13(x13_q), .in14(x14_q),
    .in15(x15_q), .in16(x16_q), .in17(x17_q), .in18(x18_q), .in19(x19_q), .in20(x20_q), .in21(x21_q),
    .in22(x22_q), .in23(x23_q), .in24(x24_q), .in25(x25_q), .in26(x26_q), .in27(x27_q), .in28(x28_q),
    .in29(x29_q), .in30(x30_q), .in31(x31_q), .out(Reg2_Out), .sel(Read_Register2));
endmodule

module ALU (
  input  [63:0] A,
  input  [63:0] B,
  input  [2:0] ALU_Op,
  input  Negate,
  input  WordFlag,
  output [63:0] Result,
  output N,
  output Z,
  output C,
  output V
);

  wire and_2_out, and_3_out, not_2_out, not_3_out, or_2_out, xnor_1_out, xor_1_out, xor_3_out, xor_4_out;
  wire [5:0] multiplexer_4_out;
  wire [31:0] shifter_3_out;
  wire [62:0] multiplexer_7_out;
  wire [63:0] ALU_Adder_s, and_1_out, bit_extender_1_out, bit_extender_2_out, bit_extender_3_out,
       bit_extender_4_out, multiplexer_1_out, multiplexer_2_out, multiplexer_3_out, multiplexer_5_out,
       multiplexer_6_out, not_1_out, or_1_out, shifter_1_out, shifter_2_out, shifter_4_out, xor_2_out;

  Multiplexer #(.width(64)) multiplexer_1 (
    .in0(A), .in1({{32{1'b0}}, A[31:0]}), .out(multiplexer_1_out), .sel(WordFlag));
  Multiplexer #(.width(64)) multiplexer_2 (
    .in0(B), .in1({{32{1'b0}}, B[31:0]}), .out(multiplexer_2_out), .sel(WordFlag));
  assign not_1_out = ~multiplexer_2_out;  // NOT_Gate not_1, 64 bits wide
  Multiplexer #(.width(64)) multiplexer_3 (
    .in0(multiplexer_2_out), .in1(not_1_out), .out(multiplexer_3_out), .sel(Negate));
  Multiplexer #(.width(6)) multiplexer_4 (
    .in0(multiplexer_2_out[5:0]), .in1({1'b0, multiplexer_2_out[4:0]}), .out(multiplexer_4_out),
    .sel(WordFlag));
  xor xor_1 (xor_1_out, ALU_Adder_s[63], V);
  not not_2 (not_2_out, C);
  Shifter #(.shift("lr"), .width(64)) shifter_1 (
    .in(multiplexer_1_out), .\dist (multiplexer_4_out), .out(shifter_1_out));
  Shifter #(.shift("ar"), .width(64)) shifter_2 (
    .in(multiplexer_1_out), .\dist (multiplexer_4_out), .out(shifter_2_out));
  Shifter #(.shift("ar"), .width(32)) shifter_3 (
    .in(multiplexer_1_out[31:0]), .\dist (multiplexer_2_out[4:0]), .out(shifter_3_out));
  Shifter #(.width(64)) shifter_4 (.in(multiplexer_1_out), .\dist (multiplexer_4_out), .out(shifter_4_out));
  assign bit_extender_1_out = {{63{1'b0}}, xor_1_out};  // Bit_Extender bit_extender_1
  assign bit_extender_2_out = {{63{1'b0}}, not_2_out};  // Bit_Extender bit_extender_2
  assign xor_2_out = multiplexer_1_out ^ multiplexer_2_out;  // XOR_Gate xor_2, 64 bits wide
  assign bit_extender_3_out = {{32{shifter_3_out[31]}}, shifter_3_out};  // Bit_Extender bit_extender_3
  assign or_1_out = multiplexer_1_out | multiplexer_2_out;  // OR_Gate or_1, 64 bits wide
  assign and_1_out = multiplexer_1_out & multiplexer_2_out;  // AND_Gate and_1, 64 bits wide
  CLA64 ALU_Adder (.A(multiplexer_1_out), .B(multiplexer_3_out), .Cin(Negate), .S(ALU_Adder_s), .Cout(C));
  Multiplexer #(.width(64)) multiplexer_5 (
    .in0(shifter_1_out), .in1(multiplexer_6_out), .out(multiplexer_5_out), .sel(Negate));
  Multiplexer #(.width(64)) multiplexer_6 (
    .in0(shifter_2_out), .in1(bit_extender_3_out), .out(multiplexer_6_out), .sel(WordFlag));
  Multiplexer #(.select(3), .width(64)) multiplexer_7 (
    .in0(ALU_Adder_s), .in1(shifter_4_out), .in2(bit_extender_1_out), .in3(bit_extender_2_out),
    .in4(xor_2_out), .in5(multiplexer_5_out), .in6(or_1_out), .in7(and_1_out), .out({N, multiplexer_7_out}),
    .sel(ALU_Op));
  assign bit_extender_4_out = {{32{multiplexer_7_out[31]}}, multiplexer_7_out[31:0]};  // Bit_Extender bit_extender_4
  xor xor_3 (xor_3_out, multiplexer_1_out[63], ALU_Adder_s[63]);
  xnor xnor_1 (xnor_1_out, multiplexer_1_out[63], multiplexer_2_out[63]);
  not not_3 (not_3_out, Negate);
  xor xor_4 (xor_4_out, multiplexer_1_out[63], multiplexer_2_out[63]);
  Multiplexer #(.width(64)) multiplexer_8 (
    .in0({N, multiplexer_7_out}), .in1(bit_extender_4_out), .out(Result), .sel(WordFlag));
  and and_2 (and_2_out, xnor_1_out, not_3_out);
  and and_3 (and_3_out, xor_4_out, Negate);
  and and_4 (V, xor_3_out, or_2_out);
  or or_2 (or_2_out, and_2_out, and_3_out);
  nor nor_1 (Z, multiplexer_7_out[0], multiplexer_7_out[1], multiplexer_7_out[2], multiplexer_7_out[3], multiplexer_7_out[4], multiplexer_7_out[5], multiplexer_7_out[6], multiplexer_7_out[7], multiplexer_7_out[8], multiplexer_7_out[9], multiplexer_7_out[10], multiplexer_7_out[11], multiplexer_7_out[12], multiplexer_7_out[13], multiplexer_7_out[14], multiplexer_7_out[15], multiplexer_7_out[16], multiplexer_7_out[17], multiplexer_7_out[18], multiplexer_7_out[19], multiplexer_7_out[20], multiplexer_7_out[21], multiplexer_7_out[22], multiplexer_7_out[23], multiplexer_7_out[24], multiplexer_7_out[25], multiplexer_7_out[26], multiplexer_7_out[27], multiplexer_7_out[28], multiplexer_7_out[29], multiplexer_7_out[30], multiplexer_7_out[31], multiplexer_7_out[32], multiplexer_7_out[33], multiplexer_7_out[34], multiplexer_7_out[35], multiplexer_7_out[36], multiplexer_7_out[37], multiplexer_7_out[38], multiplexer_7_out[39], multiplexer_7_out[40], multiplexer_7_out[41], multiplexer_7_out[42], multiplexer_7_out[43], multiplexer_7_out[44], multiplexer_7_out[45], multiplexer_7_out[46], multiplexer_7_out[47], multiplexer_7_out[48], multiplexer_7_out[49], multiplexer_7_out[50], multiplexer_7_out[51], multiplexer_7_out[52], multiplexer_7_out[53], multiplexer_7_out[54], multiplexer_7_out[55], multiplexer_7_out[56], multiplexer_7_out[57], multiplexer_7_out[58], multiplexer_7_out[59], multiplexer_7_out[60], multiplexer_7_out[61], multiplexer_7_out[62], N);

  // Notes on the sheet:
  //   ALU Opcodes
  //   000 = ADD/SUB
  //   001 = SLL
  //   010 = SLT
  //   011 = SLTU
  //   100 = XOR
  //   101 = SRL/SRA
  //   110 = OR
  //   111 = AND
  //   Negate determines whether to use B or -B or to use SRL/SRA
  //   WordFlag tells ALU to ignore upper 32 bits of inputs and produce 32-bit result (sign-extended to 64 bits)
  //   Flags
endmodule

module CLA64 (
  input  [63:0] A,
  input  [63:0] B,
  input  Cin,
  output [63:0] S,
  output Cout
);

  wire CLA4_0_cout, CLA4_1_cout, CLA4_2_cout, CLA4_3_cout, CLA4_4_cout, CLA4_5_cout, CLA4_6_cout,
       CLA4_7_cout, CLA4_8_cout, CLA4_9_cout, CLA4_10_cout, CLA4_11_cout, CLA4_12_cout, CLA4_13_cout,
       CLA4_14_cout;

  CLA4 CLA4_0 (.A(A[3:0]), .B(B[3:0]), .Cin(Cin), .S(S[3:0]), .Cout(CLA4_0_cout));
  CLA4 CLA4_1 (.A(A[7:4]), .B(B[7:4]), .Cin(CLA4_0_cout), .S(S[7:4]), .Cout(CLA4_1_cout));
  CLA4 CLA4_2 (.A(A[11:8]), .B(B[11:8]), .Cin(CLA4_1_cout), .S(S[11:8]), .Cout(CLA4_2_cout));
  CLA4 CLA4_3 (.A(A[15:12]), .B(B[15:12]), .Cin(CLA4_2_cout), .S(S[15:12]), .Cout(CLA4_3_cout));
  CLA4 CLA4_4 (.A(A[19:16]), .B(B[19:16]), .Cin(CLA4_3_cout), .S(S[19:16]), .Cout(CLA4_4_cout));
  CLA4 CLA4_5 (.A(A[23:20]), .B(B[23:20]), .Cin(CLA4_4_cout), .S(S[23:20]), .Cout(CLA4_5_cout));
  CLA4 CLA4_6 (.A(A[27:24]), .B(B[27:24]), .Cin(CLA4_5_cout), .S(S[27:24]), .Cout(CLA4_6_cout));
  CLA4 CLA4_7 (.A(A[31:28]), .B(B[31:28]), .Cin(CLA4_6_cout), .S(S[31:28]), .Cout(CLA4_7_cout));
  CLA4 CLA4_8 (.A(A[35:32]), .B(B[35:32]), .Cin(CLA4_7_cout), .S(S[35:32]), .Cout(CLA4_8_cout));
  CLA4 CLA4_9 (.A(A[39:36]), .B(B[39:36]), .Cin(CLA4_8_cout), .S(S[39:36]), .Cout(CLA4_9_cout));
  CLA4 CLA4_10 (.A(A[43:40]), .B(B[43:40]), .Cin(CLA4_9_cout), .S(S[43:40]), .Cout(CLA4_10_cout));
  CLA4 CLA4_11 (.A(A[47:44]), .B(B[47:44]), .Cin(CLA4_10_cout), .S(S[47:44]), .Cout(CLA4_11_cout));
  CLA4 CLA4_12 (.A(A[51:48]), .B(B[51:48]), .Cin(CLA4_11_cout), .S(S[51:48]), .Cout(CLA4_12_cout));
  CLA4 CLA4_13 (.A(A[55:52]), .B(B[55:52]), .Cin(CLA4_12_cout), .S(S[55:52]), .Cout(CLA4_13_cout));
  CLA4 CLA4_14 (.A(A[59:56]), .B(B[59:56]), .Cin(CLA4_13_cout), .S(S[59:56]), .Cout(CLA4_14_cout));
  CLA4 CLA4_15 (.A(A[63:60]), .B(B[63:60]), .Cin(CLA4_14_cout), .S(S[63:60]), .Cout(Cout));
endmodule

module CLA4 (
  input  [3:0] A,
  input  [3:0] B,
  input  Cin,
  output [3:0] S,
  output Cout
);

  wire and_1_out, and_2_out, and_3_out, and_4_out, and_5_out, and_6_out, and_7_out, and_8_out, and_9_out,
       and_10_out, and_11_out, and_12_out, and_13_out, and_14_out, and_15_out, and_16_out, and_17_out,
       and_18_out, and_19_out, and_20_out, FA0_cout, FA1_cout, FA2_cout, FA3_cout, or_1_out, or_2_out,
       or_3_out, or_4_out, or_5_out, or_6_out, or_7_out, or_8_out, or_9_out, xor_1_out, xor_2_out, xor_3_out,
       xor_4_out, xor_5_out, xor_6_out, xor_7_out, xor_8_out, xor_9_out, xor_10_out;

  and and_1 (and_1_out, A[0], B[0]);
  xor xor_1 (xor_1_out, A[0], B[0]);
  and and_2 (and_2_out, A[1], B[1]);
  xor xor_2 (xor_2_out, A[1], B[1]);
  and and_3 (and_3_out, A[0], B[0]);
  xor xor_3 (xor_3_out, A[0], B[0]);
  and and_4 (and_4_out, A[2], B[2]);
  xor xor_4 (xor_4_out, A[2], B[2]);
  and and_5 (and_5_out, A[1], B[1]);
  xor xor_5 (xor_5_out, A[1], B[1]);
  and and_6 (and_6_out, A[0], B[0]);
  xor xor_6 (xor_6_out, A[0], B[0]);
  and and_7 (and_7_out, A[3], B[3]);
  xor xor_7 (xor_7_out, A[3], B[3]);
  and and_8 (and_8_out, A[2], B[2]);
  xor xor_8 (xor_8_out, A[2], B[2]);
  and and_9 (and_9_out, A[1], B[1]);
  xor xor_9 (xor_9_out, A[1], B[1]);
  and and_10 (and_10_out, A[0], B[0]);
  xor xor_10 (xor_10_out, A[0], B[0]);
  and and_11 (and_11_out, xor_1_out, Cin);
  and and_12 (and_12_out, xor_3_out, Cin);
  and and_13 (and_13_out, xor_6_out, Cin);
  and and_14 (and_14_out, xor_10_out, Cin);
  or or_1 (or_1_out, and_1_out, and_11_out);
  or or_2 (or_2_out, and_3_out, and_12_out);
  or or_3 (or_3_out, and_6_out, and_13_out);
  or or_4 (or_4_out, and_10_out, and_14_out);
  and and_15 (and_15_out, xor_2_out, or_2_out);
  and and_16 (and_16_out, xor_5_out, or_3_out);
  and and_17 (and_17_out, xor_9_out, or_4_out);
  or or_5 (or_5_out, and_2_out, and_15_out);
  or or_6 (or_6_out, and_5_out, and_16_out);
  or or_7 (or_7_out, and_9_out, and_17_out);
  and and_18 (and_18_out, xor_4_out, or_6_out);
  and and_19 (and_19_out, xor_8_out, or_7_out);
  or or_8 (or_8_out, and_4_out, and_18_out);
  or or_9 (or_9_out, and_8_out, and_19_out);
  and and_20 (and_20_out, xor_7_out, or_9_out);
  or or_10 (Cout, and_7_out, and_20_out);
  Full_Adder FA0 (.A(A[0]), .B(B[0]), .Cin(Cin), .S(S[0]), .Cout(FA0_cout));
  // NoConnect on FA0_cout
  Full_Adder FA1 (.A(A[1]), .B(B[1]), .Cin(or_1_out), .S(S[1]), .Cout(FA1_cout));
  // NoConnect on FA1_cout
  Full_Adder FA2 (.A(A[2]), .B(B[2]), .Cin(or_5_out), .S(S[2]), .Cout(FA2_cout));
  // NoConnect on FA2_cout
  Full_Adder FA3 (.A(A[3]), .B(B[3]), .Cin(or_8_out), .S(S[3]), .Cout(FA3_cout));
  // NoConnect on FA3_cout

  // Notes on the sheet:
  //   C0 -->
  //   G0
  //   P0
  //   C0
  //   G1
  //   P0
  //   C0
  //   P0
  //   C0
  //   G2
  //   G1
  //   P0
  //   C0
  //   P1
  //   G0
  //   G2
  //   P2
  //   G1
  //   P1
  //   G0
  //   G3
  //   P3
  //   P2
  //   P1
  //   G0
  //   C1
  //   C1
  //   C1
  //   C0 = Cin
  //   C2
  //   C2
  //   C1 = G0 ∨ (P0 ∧ C0) = (A0 ∧ B0) ∨ ((A0 ⊕ B0) ∧ Cin)
  //   C2 = G1 ∨ (P1 ∧ C1) = (A1 ∧ B1) ∨ ((A1 ⊕ B1) ∧ ((A0 ∧ B0) ∨ ((A0 ⊕ B0) ∧ Cin)))
  //   C3
  //   C3 = G2 ∨ (P2 ∧ C2) = (A2 ∧ B2) ∨ ((A2 ⊕ B2) ∧ (A1 ∧ B1) ∨ ((A1 ⊕ B1) ∧ ((A0 ∧ B0) ∨ ((A0 ⊕ B0) ∧ Cin))))
  //   C1
  //   C2
  //   C3
  //   C4
  //   C4 = G3 ∨ (P3 ∧ C3) = (A3 ∧ B3) ∨ ((A3 ⊕ B3) ∧ ((A2 ∧ B2) ∨ ((A2 ⊕ B2) ∧ (A1 ∧ B1) ∨ ((A1 ⊕ B1) ∧ ((A0 ∧ B0) ∨ ((A0 ⊕ B0) ∧ Cin))))))
endmodule

module Full_Adder (
  input  A,
  input  B,
  input  Cin,
  output S,
  output Cout
);

  wire half_adder_1_c, half_adder_1_s, half_adder_2_c;

  Half_Adder half_adder_1 (.A(A), .B(B), .S(half_adder_1_s), .C(half_adder_1_c));
  Half_Adder half_adder_2 (.A(half_adder_1_s), .B(Cin), .S(S), .C(half_adder_2_c));
  or or_1 (Cout, half_adder_2_c, half_adder_1_c);
endmodule

module Half_Adder (
  input  A,
  input  B,
  output S,
  output C
);

  xor xor_1 (S, A, B);
  and and_1 (C, B, A);
endmodule

module Program_Memory (
  input  [63:0] PC,
  output [63:0] Instr
);

  wire [7:0] Instruction_Memory_p2, Instruction_Memory_p3, Instruction_Memory_p4, Instruction_Memory_p5;

  // ROM #(.addrWidth(16), .line("quad")) Instruction_Memory: pin names not known; wires that end beside it: PC[15:0], Instruction_Memory_p2, Instruction_Memory_p3, Instruction_Memory_p4, Instruction_Memory_p5
  assign Instr = {{32{1'b0}}, {Instruction_Memory_p5, Instruction_Memory_p4, Instruction_Memory_p3, Instruction_Memory_p2}};  // Bit_Extender bit_extender_1

  // Notes on the sheet:
  //   contents of Instruction_Memory (hex, n*v repeats v):
  //   6f 0 0 5 73 2f 20 34 93 f 80 0 63 8 ff 3 93 f 90 0 63 4 ff 3 93 f b0 0 63 0 ff 3 13 f 0 0 63 4 f 0
  //   67 0 f 0 73 2f 20 34 63 54 f 0 6f 0 40 0 93 e1 91 53 17 1f 0 0 23 22 3f fc 17 1f 0 0 23 20 f fc 6f
  //   f0 1f ff 93 0 0 0 13 1 0 0 93 1 0 0 13 2 0 0 93 2 0 0 13 3 0 0 93 3 0 0 13 4 0 0 93 4 0 0 13 5 0 0
  //   93 5 0 0 13 6 0 0 93 6 0 0 13 7 0 0 93 7 0 0 13 8 0 0 93 8 0 0 13 9 0 0 93 9 0 0 13 a 0 0 93 a 0 0
  //   13 b 0 0 93 b 0 0 13 c 0 0 93 c 0 0 13 d 0 0 93 d 0 0 13 e 0 0 93 e 0 0 13 f 0 0 93 f 0 0 73 25 40
  //   f1 63 10 5 0 97 2 0 0 93 82 2 1 73 90 52 30 73 50 44 74 97 2 0 0 93 82 2 1 73 90 52 30 73 50 0 18 97
  //   2 0 0 93 82 42 2 73 90 52 30 9b 2 10 0 93 92 52 3 93 82 f2 ff 73 90 2 3b 93 2 f0 1 73 90 2 3a 73 50
  //   40 30 97 2 0 0 93 82 42 1 73 90 52 30 73 50 20 30 73 50 30 30 93 1 0 0 97 2 0 0 93 82 2 ed 73 90 52
  //   30 13 5 10 0 13 15 f5 1 63 5c 5 0 f 0 f0 f 93 1 10 0 93 8 d0 5 13 5 0 0 73 0 0 0 93 2 0 0 63 8a 2 0
  //   73 90 52 10 b7 b2 0 0 9b 82 92 10 73 90 22 30 73 50 0 30 97 2 0 0 93 82 42 1 73 90 12 34 73 25 40 f1
  //   73 0 20 30 93 1 20 0 b7 7 ff 0 9b 87 f7 f 17 21 0 0 13 1 41 e6 3 27 1 0 b7 3 ff 0 9b 83 f3 f 63 16
  //   77 2a 93 1 30 0 b7 7 1 ff 9b 87 7 f0 17 21 0 0 13 1 1 e4 3 27 41 0 b7 3 1 ff 9b 83 3 f0 63 14 77 28
  //   93 1 40 0 b7 17 f0 f 9b 87 7 ff 17 21 0 0 13 1 c1 e1 3 27 81 0 b7 13 f0 f 9b 83 3 ff 63 12 77 26 93
  //   1 50 0 b7 f7 f f0 9b 87 f7 0 17 21 0 0 13 1 81 df 3 27 c1 0 b7 f3 f f0 9b 83 f3 0 63 10 77 24 93 1
  //   60 0 b7 7 ff 0 9b 87 f7 f 17 21 0 0 13 1 1 de 3 27 41 ff b7 3 ff 0 9b 83 f3 f 63 1e 77 20 93 1 70 0
  //   b7 7 1 ff 9b 87 7 f0 17 21 0 0 13 1 c1 db 3 27 81 ff b7 3 1 ff 9b 83 3 f0 63 1c 77 1e 93 1 80 0 b7
  //   17 f0 f 9b 87 7 ff 17 21 0 0 13 1 81 d9 3 27 c1 ff b7 13 f0 f 9b 83 3 ff 63 1a 77 1c 93 1 90 0 b7 f7
  //   f f0 9b 87 f7 0 17 21 0 0 13 1 41 d7 3 27 1 0 b7 f3 f f0 9b 83 f3 0 63 18 77 1a 93 1 a0 0 97 20 0 0
  //   93 80 c0 d4 93 80 0 fe 83 a2 0 2 b7 3 ff 0 9b 83 f3 f 63 98 72 18 93 1 b0 0 97 20 0 0 93 80 c0 d2 93
  //   80 d0 ff 83 a2 70 0 b7 3 1 ff 9b 83 3 f0 63 98 72 16 93 1 c0 0 13 2 0 0 97 26 0 0 93 86 c6 d0 3 a7
  //   46 0 13 3 7 0 b7 13 f0 f 9b 83 3 ff 63 16 73 14 13 2 12 0 93 2 20 0 e3 1e 52 fc 93 1 d0 0 13 2 0 0
  //   97 26 0 0 93 86 6 ce 3 a7 46 0 13 0 0 0 13 3 7 0 b7 f3 f f0 9b 83 f3 0 63 1c 73 10 13 2 12 0 93 2 20
  //   0 e3 1c 52 fc 93 1 e0 0 13 2 0 0 97 26 0 0 93 86 46 ca 3 a7 46 0 13 0 0 0 13 0 0 0 13 3 7 0 b7 3 1
  //   ff 9b 83 3 f0 63 10 73 e 13 2 12 0 93 2 20 0 e3 1a 52 fc 93 1 f0 0 13 2 0 0 97 26 0 0 93 86 6 c7 3
  //   a7 46 0 b7 13 f0 f 9b 83 3 ff 63 1a 77 a 13 2 12 0 93 2 20 0 e3 10 52 fe 93 1 0 1 13 2 0 0 97 26 0 0
  //   93 86 86 c4 13 0 0 0 3 a7 46 0 b7 f3 f f0 9b 83 f3 0 63 12 77 8 13 2 12 0 93 2 20 0 e3 1e 52 fc 93 1
  //   10 1 13 2 0 0 97 26 0 0 93 86 6 c1 13 0 0 0 13 0 0 0 3 a7 46 0 b7 3 1 ff 9b 83 3 f0 63 18 77 4 13 2
  //   12 0 93 2 20 0 e3 1c 52 fc 93 1 20 1 97 22 0 0 93 82 2 be 3 a1 2 0 13 1 20 0 93 3 20 0 63 14 71 2 93
  //   1 30 1 97 22 0 0 93 82 42 bc 3 a1 2 0 13 0 0 0 13 1 20 0 93 3 20 0 63 14 71 0 63 10 30 2 f 0 f0 f 63
  //   80 1 0 93 91 11 0 93 e1 11 0 93 8 d0 5 13 85 1 0 73 0 0 0 f 0 f0 f 93 1 10 0 93 8 d0 5 13 5 0 0 73 0
  //   0 0 73 10 0 c0 7024*0 ff 0 ff 0 0 ff 0 ff f0 f f0 f f f0 f f0
endmodule

module Data_Memory (
  input  Reset,
  input  Unsigned0_Signed1,
  input  [63:0] Address,
  input  Store,
  input  Load,
  input  Clock,
  input  [63:0] Data_In,
  input  [1:0] Size_Flag,
  output [63:0] Data_Out
);

  wire decoder_1_out0, decoder_1_out1, decoder_1_out2, decoder_1_out3, decoder_1_out4, decoder_1_out5,
       decoder_1_out6, decoder_1_out7, decoder_1_out8, decoder_1_out9, decoder_1_out10, decoder_1_out11,
       decoder_1_out12, decoder_1_out13, decoder_1_out14, decoder_1_out15, or_1_out;
  wire [63:0] RAM0_data_out, RAM1_data_out, RAM2_data_out, RAM3_data_out, RAM4_data_out, RAM5_data_out,
       RAM6_data_out, RAM7_data_out, RAM8_data_out, RAM9_data_out, RAM10_data_out, RAM11_data_out,
       RAM12_data_out, RAM13_data_out, RAM14_data_out, RAM15_data_out;

  or or_1 (or_1_out, Store, Load);
  Decoder #(.select(4)) decoder_1 (
    .out0(decoder_1_out0), .out1(decoder_1_out1), .out2(decoder_1_out2), .out3(decoder_1_out3),
    .out4(decoder_1_out4), .out5(decoder_1_out5), .out6(decoder_1_out6), .out7(decoder_1_out7),
    .out8(decoder_1_out8), .out9(decoder_1_out9), .out10(decoder_1_out10), .out11(decoder_1_out11),
    .out12(decoder_1_out12), .out13(decoder_1_out13), .out14(decoder_1_out14), .out15(decoder_1_out15),
    .sel(Address[27:24]), .en(or_1_out));
  RAM_Block RAM0 (
    .Unsigned0_Signed1(Unsigned0_Signed1), .Reset(Reset), .Enable(decoder_1_out0), .Load(Load),
    .Store(Store), .Size_Flag(Size_Flag), .Address(Address[23:0]), .Clock(Clock), .Data_In(Data_In),
    .Data_Out(RAM0_data_out));
  RAM_Block RAM1 (
    .Unsigned0_Signed1(Unsigned0_Signed1), .Reset(Reset), .Enable(decoder_1_out1), .Load(Load),
    .Store(Store), .Size_Flag(Size_Flag), .Address(Address[23:0]), .Clock(Clock), .Data_In(Data_In),
    .Data_Out(RAM1_data_out));
  RAM_Block RAM2 (
    .Unsigned0_Signed1(Unsigned0_Signed1), .Reset(Reset), .Enable(decoder_1_out2), .Load(Load),
    .Store(Store), .Size_Flag(Size_Flag), .Address(Address[23:0]), .Clock(Clock), .Data_In(Data_In),
    .Data_Out(RAM2_data_out));
  RAM_Block RAM3 (
    .Unsigned0_Signed1(Unsigned0_Signed1), .Reset(Reset), .Enable(decoder_1_out3), .Load(Load),
    .Store(Store), .Size_Flag(Size_Flag), .Address(Address[23:0]), .Clock(Clock), .Data_In(Data_In),
    .Data_Out(RAM3_data_out));
  RAM_Block RAM4 (
    .Unsigned0_Signed1(Unsigned0_Signed1), .Reset(Reset), .Enable(decoder_1_out4), .Load(Load),
    .Store(Store), .Size_Flag(Size_Flag), .Address(Address[23:0]), .Clock(Clock), .Data_In(Data_In),
    .Data_Out(RAM4_data_out));
  RAM_Block RAM5 (
    .Unsigned0_Signed1(Unsigned0_Signed1), .Reset(Reset), .Enable(decoder_1_out5), .Load(Load),
    .Store(Store), .Size_Flag(Size_Flag), .Address(Address[23:0]), .Clock(Clock), .Data_In(Data_In),
    .Data_Out(RAM5_data_out));
  RAM_Block RAM6 (
    .Unsigned0_Signed1(Unsigned0_Signed1), .Reset(Reset), .Enable(decoder_1_out6), .Load(Load),
    .Store(Store), .Size_Flag(Size_Flag), .Address(Address[23:0]), .Clock(Clock), .Data_In(Data_In),
    .Data_Out(RAM6_data_out));
  RAM_Block RAM7 (
    .Unsigned0_Signed1(Unsigned0_Signed1), .Reset(Reset), .Enable(decoder_1_out7), .Load(Load),
    .Store(Store), .Size_Flag(Size_Flag), .Address(Address[23:0]), .Clock(Clock), .Data_In(Data_In),
    .Data_Out(RAM7_data_out));
  RAM_Block RAM8 (
    .Unsigned0_Signed1(Unsigned0_Signed1), .Reset(Reset), .Enable(decoder_1_out8), .Load(Load),
    .Store(Store), .Size_Flag(Size_Flag), .Address(Address[23:0]), .Clock(Clock), .Data_In(Data_In),
    .Data_Out(RAM8_data_out));
  RAM_Block RAM9 (
    .Unsigned0_Signed1(Unsigned0_Signed1), .Reset(Reset), .Enable(decoder_1_out9), .Load(Load),
    .Store(Store), .Size_Flag(Size_Flag), .Address(Address[23:0]), .Clock(Clock), .Data_In(Data_In),
    .Data_Out(RAM9_data_out));
  RAM_Block RAM10 (
    .Unsigned0_Signed1(Unsigned0_Signed1), .Reset(Reset), .Enable(decoder_1_out10), .Load(Load),
    .Store(Store), .Size_Flag(Size_Flag), .Address(Address[23:0]), .Clock(Clock), .Data_In(Data_In),
    .Data_Out(RAM10_data_out));
  RAM_Block RAM11 (
    .Unsigned0_Signed1(Unsigned0_Signed1), .Reset(Reset), .Enable(decoder_1_out11), .Load(Load),
    .Store(Store), .Size_Flag(Size_Flag), .Address(Address[23:0]), .Clock(Clock), .Data_In(Data_In),
    .Data_Out(RAM11_data_out));
  RAM_Block RAM12 (
    .Unsigned0_Signed1(Unsigned0_Signed1), .Reset(Reset), .Enable(decoder_1_out12), .Load(Load),
    .Store(Store), .Size_Flag(Size_Flag), .Address(Address[23:0]), .Clock(Clock), .Data_In(Data_In),
    .Data_Out(RAM12_data_out));
  RAM_Block RAM13 (
    .Unsigned0_Signed1(Unsigned0_Signed1), .Reset(Reset), .Enable(decoder_1_out13), .Load(Load),
    .Store(Store), .Size_Flag(Size_Flag), .Address(Address[23:0]), .Clock(Clock), .Data_In(Data_In),
    .Data_Out(RAM13_data_out));
  RAM_Block RAM14 (
    .Unsigned0_Signed1(Unsigned0_Signed1), .Reset(Reset), .Enable(decoder_1_out14), .Load(Load),
    .Store(Store), .Size_Flag(Size_Flag), .Address(Address[23:0]), .Clock(Clock), .Data_In(Data_In),
    .Data_Out(RAM14_data_out));
  RAM_Block RAM15 (
    .Unsigned0_Signed1(Unsigned0_Signed1), .Reset(Reset), .Enable(decoder_1_out15), .Load(Load),
    .Store(Store), .Size_Flag(Size_Flag), .Address(Address[23:0]), .Clock(Clock), .Data_In(Data_In),
    .Data_Out(RAM15_data_out));
  Multiplexer #(.enable("true"), .select(4), .width(64)) multiplexer_1 (
    .in0(RAM0_data_out), .in1(RAM1_data_out), .in2(RAM2_data_out), .in3(RAM3_data_out), .in4(RAM4_data_out),
    .in5(RAM5_data_out), .in6(RAM6_data_out), .in7(RAM7_data_out), .in8(RAM8_data_out), .in9(RAM9_data_out),
    .in10(RAM10_data_out), .in11(RAM11_data_out), .in12(RAM12_data_out), .in13(RAM13_data_out),
    .in14(RAM14_data_out), .in15(RAM15_data_out), .out(Data_Out), .sel(Address[27:24]), .en(Load));

  // Notes on the sheet:
  //   Size Flags
  //   00 = Store/Load Byte
  //   01 = Store/Load Half Word
  //   10 = Store/Load Word
  //   11 = Store/Load Long Word
  //   2^32 addresses per byte = 4GB total
  //   Implementing the entire 4GB range is unreasonable as that requires 256 RAM blocks
  //   To make this more reasonable, I'm addressing only 16 RAM blocks (4 address bits)
  //   This totals my data memory unit to 256 MB
endmodule

module RAM_Block (
  input  Unsigned0_Signed1,
  input  Reset,
  input  Enable,
  input  Load,
  input  Store,
  input  [1:0] Size_Flag,
  input  [23:0] Address,
  input  Clock,
  input  [63:0] Data_In,
  output [63:0] Data_Out
);

  wire and_1_out, and_2_out, and_3_out, and_4_out, and_5_out, or_1_out;
  wire [7:0] DMemBlock_p21, DMemBlock_p22, DMemBlock_p23, DMemBlock_p24, DMemBlock_p25, DMemBlock_p26,
       DMemBlock_p27, DMemBlock_p28, multiplexer_1_out;
  wire [63:0] bit_extender_1_out, bit_extender_2_out, bit_extender_3_out;

  and and_1 (and_1_out, Enable, Load);
  and and_2 (and_2_out, Enable, Store);
  or or_1 (or_1_out, and_1_out, and_2_out);
  Multiplexer #(.enable("true"), .select(2), .width(8)) multiplexer_1 (
    .in0(8'h1), .in1(8'h3), .in2(8'hf), .in3({8{1'b1}}), .out(multiplexer_1_out), .sel(Size_Flag),
    .en(or_1_out));
  // RAM #(.addrWidth(24), .clearpin("true"), .enables("line"), .line("octo"), .misaligned("true")) DMemBlock: pin names not known; wires that end beside it: Address, and_2_out, multiplexer_1_out[0], multiplexer_1_out[1], multiplexer_1_out[2], multiplexer_1_out[3], multiplexer_1_out[4], multiplexer_1_out[5], multiplexer_1_out[6], multiplexer_1_out[7], Clock, Data_In[7:0], Data_In[15:8], Data_In[23:16], Data_In[31:24], Data_In[39:32], Data_In[47:40], Data_In[55:48], Data_In[63:56], Reset, DMemBlock_p21, DMemBlock_p22, DMemBlock_p23, DMemBlock_p24, DMemBlock_p25, DMemBlock_p26, DMemBlock_p27, DMemBlock_p28
  and and_3 (and_3_out, Unsigned0_Signed1, DMemBlock_p21[7]);
  and and_4 (and_4_out, Unsigned0_Signed1, DMemBlock_p22[7]);
  and and_5 (and_5_out, Unsigned0_Signed1, DMemBlock_p24[7]);
  assign bit_extender_1_out = {{56{and_3_out}}, DMemBlock_p21};  // Bit_Extender bit_extender_1
  assign bit_extender_2_out = {{48{and_4_out}}, {DMemBlock_p22, DMemBlock_p21}};  // Bit_Extender bit_extender_2
  assign bit_extender_3_out = {{32{and_5_out}}, {DMemBlock_p24, DMemBlock_p23, DMemBlock_p22, DMemBlock_p21}};  // Bit_Extender bit_extender_3
  Multiplexer #(.enable("true"), .select(2), .width(64)) multiplexer_2 (
    .in0(bit_extender_1_out), .in1(bit_extender_2_out), .in2(bit_extender_3_out),
    .in3({DMemBlock_p28, DMemBlock_p27, DMemBlock_p26, DMemBlock_p25, DMemBlock_p24, DMemBlock_p23, DMemBlock_p22, DMemBlock_p21}),
    .out(Data_Out), .sel(Size_Flag), .en(and_1_out));

  // Notes on the sheet:
  //   Size Flags
  //   00 = Store/Load Byte
  //   01 = Store/Load Half Word
  //   10 = Store/Load Word
  //   11 = Store/Load Long Word
  //   This RAM Block handles up to 64 bits (8 bytes) per store or load.
  //   The Size Flag input determines whether to store/load a byte, half word, word, or long word
  //   Handles address up to 24 bits, totalling to 16 MB per RAM block
endmodule
