// Logisim project risc_v_darkstar.circ as structural Verilog: 11 circuits, main circuit main
module main (
  input  Reset,
  input  in_2
);

  wire adder_1_cout, Clock_Gen_out_1, Control_Unit_alu_enable, Control_Unit_alu_sign, undriven;
  wire [3:0] Control_Unit_alu_op;
  wire [4:0] Control_Unit_dest_reg;
  wire [12:0] PC_data_out;
  wire [63:0] adder_1_out, alu_block_1_result, bit_extender_1_out, Control_Unit_alu_a, Control_Unit_alu_b;

  Clock_Generator Clock_Gen (.out_1(Clock_Gen_out_1));
  // Probe on adder_1_out
  Program_Counter PC (.Reset(Reset), .Clock(Clock_Gen_out_1), .Data_In(adder_1_out), .Data_Out(PC_data_out));
  assign bit_extender_1_out = {{51{1'b0}}, PC_data_out};  // Bit_Extender bit_extender_1
  // NoConnect on undriven
  Adder #(.width(64)) adder_1 (
    .a(bit_extender_1_out), .b(64'h1), .out(adder_1_out), .cin(undriven), .cout(adder_1_cout));
  // NoConnect on adder_1_cout
  Instruction_Memory Instruction_Cache (
    .Address(PC_data_out), .Write(in_2), .Clock(Clock_Gen_out_1), .Data_In(64'h81923829));  // open: Instruction
  Control_Block Control_Unit (
    .Instruction(64'h37dee237), .Dest_Reg(Control_Unit_dest_reg), .ALU_Enable(Control_Unit_alu_enable),
    .ALU_Sign(Control_Unit_alu_sign), .ALU_Op(Control_Unit_alu_op), .ALU_A(Control_Unit_alu_a),
    .ALU_B(Control_Unit_alu_b));  // open: Immediate
  Register_Block Registers (
    .Reset(Reset), .Data(alu_block_1_result), .Destination_Register(Control_Unit_dest_reg));  // open: Write, Clock, Source_Register1, Source_Register2, Src_Out1, Src_Out2
  ALU_Block alu_block_1 (
    .Enable(Control_Unit_alu_enable), .Sign_Flag(Control_Unit_alu_sign), .Op(Control_Unit_alu_op),
    .Operand1(Control_Unit_alu_a), .Operand2(Control_Unit_alu_b), .Result(alu_block_1_result));  // open: Greater, Equal, Lesser
  Data_Memory Data_Cache ();  // open: Address, Write, Read, Clock, Data_In, Data_Out
endmodule

module Clock_Generator (
  output out_1
);

  Clock clock_1 (.out(out_1));
endmodule

module ALU_Block (
  input  Enable,
  input  Sign_Flag,
  input  [3:0] Op,
  input  [63:0] Operand1,
  input  [63:0] Operand2,
  output [63:0] Result,
  output Greater,
  output Equal,
  output Lesser
);

  wire comparator_1_eq, comparator_1_gt, comparator_1_lt, comparator_2_eq, comparator_2_gt, comparator_2_lt;
  wire [63:0] adder_1_out, and_1_out, or_1_out, shifter_1_out, shifter_2_out, shifter_3_out, shifter_4_out,
       shifter_5_out, subtractor_1_out, xor_1_out;

  // NoConnect on Operand2[63:6]
  Adder #(.width(64)) adder_1 (.a(Operand1), .b(Operand2), .out(adder_1_out));  // open: cin, cout
  Subtractor #(.width(64)) subtractor_1 (.a(Operand1), .b(Operand2), .out(subtractor_1_out));  // open: bin, bout
  Comparator #(.width(64)) comparator_1 (
    .a(Operand1), .b(Operand2), .gt(comparator_1_gt), .eq(comparator_1_eq), .lt(comparator_1_lt));
  Shifter #(.width(64)) shifter_1 (.in(Operand1), .\dist (Operand2[5:0]), .out(shifter_1_out));
  Shifter #(.shift("lr"), .width(64)) shifter_2 (.in(Operand1), .\dist (Operand2[5:0]), .out(shifter_2_out));
  Shifter #(.shift("ar"), .width(64)) shifter_3 (.in(Operand1), .\dist (Operand2[5:0]), .out(shifter_3_out));
  Shifter #(.shift("rl"), .width(64)) shifter_4 (.in(Operand1), .\dist (Operand2[5:0]), .out(shifter_4_out));
  Shifter #(.shift("rr"), .width(64)) shifter_5 (.in(Operand1), .\dist (Operand2[5:0]), .out(shifter_5_out));
  Comparator #(.mode("unsigned"), .width(64)) comparator_2 (
    .a(Operand1), .b(Operand2), .gt(comparator_2_gt), .eq(comparator_2_eq), .lt(comparator_2_lt));
  assign or_1_out = Operand1 | Operand2;  // OR_Gate or_1, 64 bits wide
  assign xor_1_out = Operand1 ^ Operand2;  // XOR_Gate xor_1, 64 bits wide
  assign and_1_out = Operand1 & Operand2;  // AND_Gate and_1, 64 bits wide
  Multiplexer #(.enable("true"), .select(4), .width(64)) multiplexer_1 (
    .in0(adder_1_out), .in1(subtractor_1_out), .in2(or_1_out), .in3(xor_1_out), .in4(and_1_out),
    .in5(shifter_1_out), .in6(shifter_2_out), .in7(shifter_3_out), .in8(shifter_4_out), .in9(shifter_5_out),
    .in10({64{1'b0}}), .in11({64{1'b0}}), .in12({64{1'b0}}), .in13({64{1'b0}}), .in14({64{1'b0}}),
    .in15({64{1'b0}}), .out(Result), .sel(Op), .en(Enable));
  Multiplexer #(.enable("true")) multiplexer_2 (
    .in0(comparator_1_gt), .in1(comparator_2_gt), .out(Greater), .sel(Sign_Flag), .en(Enable));
  Multiplexer #(.enable("true")) multiplexer_3 (
    .in0(comparator_1_eq), .in1(comparator_2_eq), .out(Equal), .sel(Sign_Flag), .en(Enable));
  Multiplexer #(.enable("true")) multiplexer_4 (
    .in0(comparator_1_lt), .in1(comparator_2_lt), .out(Lesser), .sel(Sign_Flag), .en(Enable));
endmodule

module Control_Block (
  input  [63:0] Instruction,
  output [4:0] Dest_Reg,
  output ALU_Enable,
  output ALU_Sign,
  output [3:0] ALU_Op,
  output [63:0] ALU_A,
  output [63:0] ALU_B,
  output [63:0] Immediate
);

  wire comparator_1_eq, nor_1_out;

  // NoConnect on Instruction[63:32]
  Comparator #(.mode("unsigned"), .width(7)) comparator_1 (
    .a(7'b0110111), .b(Instruction[6:0]), .eq(comparator_1_eq));  // open: gt, lt
  nor nor_1 (nor_1_out, 1'b0, comparator_1_eq);
  Invalid invalid_1 (
    .Enable(nor_1_out), .Dest_Reg(Dest_Reg), .ALU_Enable(ALU_Enable), .ALU_Sign(ALU_Sign), .ALU_Op(ALU_Op),
    .ALU_A(ALU_A), .ALU_B(ALU_B), .Immediate(Immediate));
  LUI_Control_Block LUI (
    .Enable(comparator_1_eq), .Data(Instruction[31:7]), .Dest_Reg(Dest_Reg), .ALU_Enable(ALU_Enable),
    .ALU_Sign(ALU_Sign), .ALU_Op(ALU_Op), .ALU_A(ALU_A), .ALU_B(ALU_B), .Immediate(Immediate));

  // Notes on the sheet:
  //   Invalid Instruction
  //   Load Upper Immediate
endmodule

module Register_Block (
  input  Write,
  input  Reset,
  input  Clock,
  input  [63:0] Data,
  input  [4:0] Source_Register1,
  input  [4:0] Source_Register2,
  input  [4:0] Destination_Register,
  output [63:0] Src_Out1,
  output [63:0] Src_Out2
);

  wire decoder_1_out1, decoder_1_out2, decoder_1_out3, decoder_1_out4, decoder_1_out5, decoder_1_out6,
       decoder_1_out7, decoder_1_out8, decoder_1_out9, decoder_1_out10, decoder_1_out11, decoder_1_out12,
       decoder_1_out13, decoder_1_out14, decoder_1_out15, decoder_1_out16, decoder_1_out17, decoder_1_out18,
       decoder_1_out19, decoder_1_out20, decoder_1_out21, decoder_1_out22, decoder_1_out23, decoder_1_out24,
       decoder_1_out25, decoder_1_out26, decoder_1_out27, decoder_1_out28, decoder_1_out29, decoder_1_out30,
       decoder_1_out31, undriven_2;
  wire [63:0] register_1_q, register_2_q, register_3_q, register_4_q, register_5_q, register_6_q,
       register_7_q, register_8_q, register_9_q, register_10_q, register_11_q, register_12_q, register_13_q,
       register_14_q, register_15_q, register_16_q, register_17_q, register_18_q, register_19_q,
       register_20_q, register_21_q, register_22_q, register_23_q, register_24_q, register_25_q,
       register_26_q, register_27_q, register_28_q, register_29_q, register_30_q, register_31_q,
       register_32_q, undriven;

  Decoder #(.select(5)) decoder_1 (
    .out1(decoder_1_out1), .out2(decoder_1_out2), .out3(decoder_1_out3), .out4(decoder_1_out4),
    .out5(decoder_1_out5), .out6(decoder_1_out6), .out7(decoder_1_out7), .out8(decoder_1_out8),
    .out9(decoder_1_out9), .out10(decoder_1_out10), .out11(decoder_1_out11), .out12(decoder_1_out12),
    .out13(decoder_1_out13), .out14(decoder_1_out14), .out15(decoder_1_out15), .out16(decoder_1_out16),
    .out17(decoder_1_out17), .out18(decoder_1_out18), .out19(decoder_1_out19), .out20(decoder_1_out20),
    .out21(decoder_1_out21), .out22(decoder_1_out22), .out23(decoder_1_out23), .out24(decoder_1_out24),
    .out25(decoder_1_out25), .out26(decoder_1_out26), .out27(decoder_1_out27), .out28(decoder_1_out28),
    .out29(decoder_1_out29), .out30(decoder_1_out30), .out31(decoder_1_out31), .sel(Destination_Register),
    .en(Write));  // open: out0
  Register #(.width(64)) register_1 (.D(undriven), .en(undriven_2), .clk(Clock), .Q(register_1_q), .clr(Reset));
  // NoConnect on undriven
  // NoConnect on undriven_2
  Register #(.width(64)) register_2 (.D(Data), .en(decoder_1_out1), .clk(Clock), .Q(register_2_q), .clr(Reset));
  Register #(.width(64)) register_3 (.D(Data), .en(decoder_1_out2), .clk(Clock), .Q(register_3_q), .clr(Reset));
  Register #(.width(64)) register_4 (.D(Data), .en(decoder_1_out3), .clk(Clock), .Q(register_4_q), .clr(Reset));
  Register #(.width(64)) register_5 (.D(Data), .en(decoder_1_out4), .clk(Clock), .Q(register_5_q), .clr(Reset));
  Register #(.width(64)) register_6 (.D(Data), .en(decoder_1_out5), .clk(Clock), .Q(register_6_q), .clr(Reset));
  Register #(.width(64)) register_7 (.D(Data), .en(decoder_1_out6), .clk(Clock), .Q(register_7_q), .clr(Reset));
  Register #(.width(64)) register_8 (.D(Data), .en(decoder_1_out7), .clk(Clock), .Q(register_8_q), .clr(Reset));
  Register #(.width(64)) register_9 (.D(Data), .en(decoder_1_out8), .clk(Clock), .Q(register_9_q), .clr(Reset));
  Register #(.width(64)) register_10 (.D(Data), .en(decoder_1_out9), .clk(Clock), .Q(register_10_q), .clr(Reset));
  Register #(.width(64)) register_11 (.D(Data), .en(decoder_1_out10), .clk(Clock), .Q(register_11_q), .clr(Reset));
  Register #(.width(64)) register_12 (.D(Data), .en(decoder_1_out11), .clk(Clock), .Q(register_12_q), .clr(Reset));
  Register #(.width(64)) register_13 (.D(Data), .en(decoder_1_out12), .clk(Clock), .Q(register_13_q), .clr(Reset));
  Register #(.width(64)) register_14 (.D(Data), .en(decoder_1_out13), .clk(Clock), .Q(register_14_q), .clr(Reset));
  Register #(.width(64)) register_15 (.D(Data), .en(decoder_1_out14), .clk(Clock), .Q(register_15_q), .clr(Reset));
  Register #(.width(64)) register_16 (.D(Data), .en(decoder_1_out15), .clk(Clock), .Q(register_16_q), .clr(Reset));
  Register #(.width(64)) register_17 (.D(Data), .en(decoder_1_out16), .clk(Clock), .Q(register_17_q), .clr(Reset));
  Register #(.width(64)) register_18 (.D(Data), .en(decoder_1_out17), .clk(Clock), .Q(register_18_q), .clr(Reset));
  Register #(.width(64)) register_19 (.D(Data), .en(decoder_1_out18), .clk(Clock), .Q(register_19_q), .clr(Reset));
  Register #(.width(64)) register_20 (.D(Data), .en(decoder_1_out19), .clk(Clock), .Q(register_20_q), .clr(Reset));
  Register #(.width(64)) register_21 (.D(Data), .en(decoder_1_out20), .clk(Clock), .Q(register_21_q), .clr(Reset));
  Register #(.width(64)) register_22 (.D(Data), .en(decoder_1_out21), .clk(Clock), .Q(register_22_q), .clr(Reset));
  Register #(.width(64)) register_23 (.D(Data), .en(decoder_1_out22), .clk(Clock), .Q(register_23_q), .clr(Reset));
  Register #(.width(64)) register_24 (.D(Data), .en(decoder_1_out23), .clk(Clock), .Q(register_24_q), .clr(Reset));
  Register #(.width(64)) register_25 (.D(Data), .en(decoder_1_out24), .clk(Clock), .Q(register_25_q), .clr(Reset));
  Register #(.width(64)) register_26 (.D(Data), .en(decoder_1_out25), .clk(Clock), .Q(register_26_q), .clr(Reset));
  Register #(.width(64)) register_27 (.D(Data), .en(decoder_1_out26), .clk(Clock), .Q(register_27_q), .clr(Reset));
  Register #(.width(64)) register_28 (.D(Data), .en(decoder_1_out27), .clk(Clock), .Q(register_28_q), .clr(Reset));
  Register #(.width(64)) register_29 (.D(Data), .en(decoder_1_out28), .clk(Clock), .Q(register_29_q), .clr(Reset));
  Register #(.width(64)) register_30 (.D(Data), .en(decoder_1_out29), .clk(Clock), .Q(register_30_q), .clr(Reset));
  Register #(.width(64)) register_31 (.D(Data), .en(decoder_1_out30), .clk(Clock), .Q(register_31_q), .clr(Reset));
  Register #(.width(64)) register_32 (.D(Data), .en(decoder_1_out31), .clk(Clock), .Q(register_32_q), .clr(Reset));
  Multiplexer #(.select(5), .width(64)) multiplexer_1 (
    .in0(register_1_q), .in1(register_2_q), .in2(register_3_q), .in3(register_4_q), .in4(register_5_q),
    .in5(register_6_q), .in6(register_7_q), .in7(register_8_q), .in8(register_9_q), .in9(register_10_q),
    .in10(register_11_q), .in11(register_12_q), .in12(register_13_q), .in13(register_14_q),
    .in14(register_15_q), .in15(register_16_q), .in16(register_17_q), .in17(register_18_q),
    .in18(register_19_q), .in19(register_20_q), .in20(register_21_q), .in21(register_22_q),
    .in22(register_23_q), .in23(register_24_q), .in24(register_25_q), .in25(register_26_q),
    .in26(register_27_q), .in27(register_28_q), .in28(register_29_q), .in29(register_30_q),
    .in30(register_31_q), .in31(register_32_q), .out(Src_Out1), .sel(Source_Register1));
  Multiplexer #(.select(5), .width(64)) multiplexer_2 (
    .in0(register_1_q), .in1(register_2_q), .in2(register_3_q), .in3(register_4_q), .in4(register_5_q),
    .in5(register_6_q), .in6(register_7_q), .in7(register_8_q), .in8(register_9_q), .in9(register_10_q),
    .in10(register_11_q), .in11(register_12_q), .in12(register_13_q), .in13(register_14_q),
    .in14(register_15_q), .in15(register_16_q), .in16(register_17_q), .in17(register_18_q),
    .in18(register_19_q), .in19(register_20_q), .in20(register_21_q), .in21(register_22_q),
    .in22(register_23_q), .in23(register_24_q), .in24(register_25_q), .in25(register_26_q),
    .in26(register_27_q), .in27(register_28_q), .in28(register_29_q), .in29(register_30_q),
    .in30(register_31_q), .in31(register_32_q), .out(Src_Out2), .sel(Source_Register2));
endmodule

module Program_Counter (
  input  Reset,
  input  Clock,
  input  [63:0] Data_In,
  output [12:0] Data_Out
);

  wire Program_Counter_carry, undriven, undriven_2;
  wire [63:13] Program_Counter_q;

  Counter #(.max('hffffffffffffffff), .width(64)) Program_Counter (
    .clr(Reset), .load(1'b1), .up(undriven), .count(undriven_2), .clk(Clock), .D(Data_In),
    .carry(Program_Counter_carry), .Q({Program_Counter_q, Data_Out}));
  // NoConnect on undriven
  // NoConnect on undriven_2
  // NoConnect on Program_Counter_carry
  // NoConnect on Program_Counter_q
endmodule

module Instruction_Memory (
  input  [12:0] Address,
  input  Write,
  input  Clock,
  input  [63:0] Data_In,
  output [63:0] Instruction
);

  RAM #(.addrWidth(13), .dataWidth(64)) Instruction_Cache (
    .addr(Address), .we(Write), .oe(1'b1), .clk(Clock), .din(Data_In), .dout(Instruction));
endmodule

module Data_Memory (
  input  [63:0] Address,
  input  Write,
  input  Read,
  input  Clock,
  input  [63:0] Data_In,
  output [63:0] Data_Out
);

  RAM #(.addrWidth(17), .dataWidth(64)) ram_1 (
    .addr(Address[16:0]), .we(Write), .oe(Read), .clk(Clock), .din(Data_In), .dout(Data_Out));
endmodule

module Branch_Control (
  input  Less_Enable,
  input  Less,
  input  Equal_Enable,
  input  Equal,
  input  More_Enable,
  input  More,
  input  Not_Equal_Enable,
  output Branch
);

  wire and_1_out, and_2_out, and_3_out, and_4_out, not_1_out;

  and and_1 (and_1_out, Less_Enable, Less);
  and and_2 (and_2_out, Equal_Enable, Equal);
  not not_1 (not_1_out, Equal);
  and and_3 (and_3_out, More_Enable, More);
  and and_4 (and_4_out, Not_Equal_Enable, not_1_out);
  or or_1 (Branch, and_1_out, and_2_out, and_3_out, and_4_out);
endmodule

module LUI_Control_Block (
  input  Enable,
  input  [24:0] Data,
  output [4:0] Dest_Reg,
  output ALU_Enable,
  output ALU_Sign,
  output [3:0] ALU_Op,
  output [63:0] ALU_A,
  output [63:0] ALU_B,
  output [63:0] Immediate
);

  wire [63:0] bit_extender_1_out;

  assign bit_extender_1_out = {{44{Data[24]}}, Data[24:5]};  // Bit_Extender bit_extender_1
  assign Dest_Reg = Enable ? Data[4:0] : 5'bz;  // Controlled_Buffer controlled_buffer_1
  assign ALU_Enable = Enable ? 1'b1 : 1'bz;  // Controlled_Buffer controlled_buffer_2
  assign ALU_Sign = Enable ? 1'b0 : 1'bz;  // Controlled_Buffer controlled_buffer_3
  assign ALU_Op = Enable ? 4'b0101 : 4'bz;  // Controlled_Buffer controlled_buffer_4
  assign ALU_A = Enable ? bit_extender_1_out : 64'bz;  // Controlled_Buffer controlled_buffer_5
  assign ALU_B = Enable ? 64'hc : 64'bz;  // Controlled_Buffer controlled_buffer_6
  assign Immediate = Enable ? {64{1'b0}} : 64'bz;  // Controlled_Buffer controlled_buffer_7
endmodule

module Invalid (
  input  Enable,
  output [4:0] Dest_Reg,
  output ALU_Enable,
  output ALU_Sign,
  output [3:0] ALU_Op,
  output [63:0] ALU_A,
  output [63:0] ALU_B,
  output [63:0] Immediate
);

  wire [3:0] bit_extender_2_out;
  wire [4:0] bit_extender_1_out;
  wire [63:0] bit_extender_3_out;

  assign bit_extender_1_out = {{4{1'b0}}, 1'b0};  // Bit_Extender bit_extender_1
  assign bit_extender_2_out = {{3{1'b0}}, 1'b0};  // Bit_Extender bit_extender_2
  assign bit_extender_3_out = {{63{1'b0}}, 1'b0};  // Bit_Extender bit_extender_3
  assign Dest_Reg = Enable ? bit_extender_1_out : 5'bz;  // Controlled_Buffer controlled_buffer_1
  assign ALU_Enable = Enable ? 1'b0 : 1'bz;  // Controlled_Buffer controlled_buffer_2
  assign ALU_Sign = Enable ? 1'b0 : 1'bz;  // Controlled_Buffer controlled_buffer_3
  assign ALU_Op = Enable ? bit_extender_2_out : 4'bz;  // Controlled_Buffer controlled_buffer_4
  assign ALU_A = Enable ? bit_extender_3_out : 64'bz;  // Controlled_Buffer controlled_buffer_5
  assign ALU_B = Enable ? bit_extender_3_out : 64'bz;  // Controlled_Buffer controlled_buffer_6
  assign Immediate = Enable ? bit_extender_3_out : 64'bz;  // Controlled_Buffer controlled_buffer_7
endmodule
